# Fritzing sketch Untitled Sketch 3 (saved by Fritzing 0.9.3b)
breadboards: 1

parts:
  R1 = Resistor [tolerance=±5% resistance=220 package=THT]
  R2 = Photocell (LDR) [package=THT]
  DHT1 = DHT22 Humidity and Temperature Sensor
  Componente2 = FC-28 Soil Hygrometer Module
  Componente3 = FC-28 Soil Hygrometer Module - Probe
  Componente1 = Arduino Mega 2560 (Rev3)
  Componente4 = Solid State High Level Relay Module [package=relay]
  M1 = DC Motor

nets:
  N1: R1.Pin_0, R2.pin_1, Componente1.A0
  GND: R1.Pin_1, DHT1.GND, Componente2.GND, Componente1.GND
  VDD: R2.pin_0, DHT1.VDD, Componente2.VCC, Componente1.5V
  N2: DHT1.DATA, Componente1.D3_PWM
  N3: Componente2.AO, Componente1.A3
  N4: Componente2.POS, Componente3.POS
  N5: Componente2.NEG, Componente3.NEG
  N6: Componente4.B1, M1.pin_2

custom parts:
  FC-28 Soil Hygrometer Module: The FC-28 is a soil hygrometer module that uses the Texas Instruments LM393 comparator chip to provide an analog measurement of soil humidity. The digital output is high when soil moisture is over a certain threshold, as determined by adjusting the potentiometer.
  FC-28 Soil Hygrometer Module - Probe: The FC-28 is a soil hygrometer module that uses the Texas Instruments LM393 comparator chip to provide an analog measurement of soil humidity.
  Solid State High Level Relay Module: 5V Omron solid state relay 240V 2A output with resistance fuse.
